# Fritzing sketch BeachSafety_v2_sender_radiohead (saved by Fritzing 0.9.3b)

parts:
  Part1 = Arduino Nano (Rev3.0)
  Part5 = Arduino Nano (Rev3.0) (ICSP)
  U2 = UBLOX NEO 6M GPS
  S1 = Toggle Switch [package=THT]
  S2 = Toggle Switch [package=THT]
  U5 = LIPO-1000mAh [package=lipo-1000]
  U6 = LIPO-1000mAh [package=lipo-1000]
  JP2 = USB_MICROB_PLUG [package=micro-b-ra-th]
  Part6 = NRF905 Stub [chip_label=NRF905 package=SO]
  JP1 = USB_MICROB_PLUG [package=micro-b-ra-th]
  U4 = LIPO-1000mAh [package=lipo-1000]
  U3 = LIPO-1000mAh [package=lipo-1000]

nets:
  N1: Part1.D1/TX, S1.L2
  N2: Part1.D0/RX, S2.L2
  GND: Part1.GND, Part5.GND, Part6.GND_13, Part6.GND_14
  N3: Part1.D8, Part6.TRAXCE
  N4: Part1.D9, Part6.TXEN
  N5: Part1.D10, Part6.CSN
  3V3: Part1.3V3, Part6.VCC
  N6: Part5.D1/TX, S2.COM
  N7: Part5.D0/RX, S1.COM
  N8: Part5.D8, U2.TXD, U2.GND
  N9: Part5.D9, U2.RXD
  3V3_2: Part5.3V3, U2.VCC
  N10: U5.+, U6.-
  N11: U5.-, JP2.D-, JP2.D+
  N12: U6.+, JP2.VCC
  N13: JP1.VCC, JP1.D-, U3.+
  N14: JP1.D+, U4.-
  N15: U4.+, U3.-

notes:
  Need two Arduinos, too many gadgets.
  Connect batteries in series to get over 5v.
  Power via USB and the Ardunio will regulate the voltage.
  Disconnect Arduinos when uploading code.

custom parts:
  UBLOX NEO 6M GPS: uSD module
  NRF905 Stub: A stub graphic for the NRF905 RF so I can get this project done. The graphic does not look like the product, but it has the correct number of pins in the correct order.
