# Fritzing sketch BeachSafety_v2_sender_zak_lib (saved by Fritzing 0.9.3b)

parts:
  Part1 = Arduino Nano (Rev3.0)
  Part5 = Arduino Nano (Rev3.0) (ICSP)
  U2 = UBLOX NEO 6M GPS
  S1 = Toggle Switch [package=THT]
  S2 = Toggle Switch [package=THT]
  U3 = LIPO-1000mAh [package=lipo-1000]
  U4 = LIPO-1000mAh [package=lipo-1000]
  JP1 = USB_MICROB_PLUG [package=micro-b-ra-th]
  U5 = LIPO-1000mAh [package=lipo-1000]
  U6 = LIPO-1000mAh [package=lipo-1000]
  JP2 = USB_MICROB_PLUG [package=micro-b-ra-th]
  Part4 = NRF905 Stub [chip_label=NRF905 package=SO]

nets:
  N1: Part1.D1/TX, S1.L2
  N2: Part1.D0/RX, S2.L2
  GND: Part1.GND, Part5.GND, Part4.GND_13, Part4.GND_14
  N3: Part1.D2, Part4.AM
  N4: Part1.D3, Part4.DR
  N5: Part1.D4, Part4.CD
  N6: Part1.D7, Part4.TRAXCE
  N7: Part1.D8, Part4.PW_UP
  N8: Part1.D9, Part4.TXEN
  N9: Part1.D10, Part4.CSN
  N10: Part1.D11/MOSI, Part4.MOSI
  N11: Part1.D12/MISO, Part4.MISO
  3V3: Part1.3V3, Part4.VCC
  N12: Part1.D13/SCK, Part4.SCK
  N13: Part5.D1/TX, S2.COM
  N14: Part5.D0/RX, S1.COM
  N15: Part5.D8, U2.TXD, U2.GND
  N16: Part5.D9, U2.RXD
  3V3_2: Part5.3V3, U2.VCC
  N17: U3.+, JP1.VCC, JP1.D-
  N18: U3.-, U4.+
  N19: U4.-, JP1.D+
  N20: U5.+, U6.-
  N21: U5.-, JP2.D-, JP2.D+
  N22: U6.+, JP2.VCC

notes:
  Need two Arduinos, too many gadgets.
  Connect batteries in series to get over 5v.
  Power via USB and the Ardunio will regulate the voltage.
  Disconnect Arduinos when uploading code.
  UGH, the labels don't match my chip

custom parts:
  UBLOX NEO 6M GPS: uSD module
  NRF905 Stub: A stub graphic for the NRF905 RF so I can get this project done. The graphic does not look like the product, but it has the correct number of pins in the correct order.
